// Logisim project cpu.circ as structural Verilog
module CPU (
  input  [31:0] Instruction,
  input  CLK,
  output [31:0] s0,
  output [31:0] s1,
  output [31:0] t0,
  output [31:0] t1,
  output [31:0] a0,
  output [31:0] ra,
  output [31:0] sp,
  output [31:0] PC
);

  // Incrementer incrementer_1: pin names not known
  // PC pc_1: pin names not known; wires that end beside it: CLK
  RegFile regfile_1 (
    .Clk(CLK), .RD(Instruction[11:7]), .RS1(Instruction[19:15]), .RS2(Instruction[24:20]), .s0(s0), .s1(s1),
    .t0(t0), .t1(t1), .a0(a0), .ra(ra), .sp(sp));  // open: R1, R2, WE, W
  ImmGenerator immgenerator_1 ();
  // ALU alu_1: pin names not known
  // memory_main main_1: pin names not known; wires that end beside it: CLK

  // Other names for the same wires on the sheet: fetch_addr[31:0] = PC; INST[31:0] = Instruction;
  //   rd[4:0] = Instruction[11:7]; rs1[4:0] = Instruction[19:15]; rs2[4:0] = Instruction[24:20]

  // Notes on the sheet:
  //   NOTE
  //   Please do not modify/replace/move/change/delete/etc input and output pins
  //   These are debug/test outputs from your circuit
endmodule

module control (
);

  wire comparator_1_eq, comparator_2_eq;
  wire [6:0] opcode;

  Comparator #(.width(7)) comparator_1 (.a(opcode), .b(7'b0110011), .eq(comparator_1_eq));  // open: gt, lt
  Comparator #(.width(7)) comparator_2 (.a(opcode), .b(7'b0010011), .eq(comparator_2_eq));  // open: gt, lt
endmodule
